// Digital circuit brainless.dig as structural Verilog
module brainless (
  input  invert,
  input  arith,
  input  pass,
  input  load__acc,
  input  acc__to__db,
  input  reset,
  input  clk,
  input  write,
  input  read,
  input  [3:0] addr__bus,
  input  [3:0] data__in,
  output [3:0] data__bus,
  output [3:0] accum,
  output [3:0] alu__out
);

  wire accum__mux_p1;
  wire [3:0] program_ram_1_data__out;

  // alu alu_1: pin names not known; wires that end beside it: data__bus, accum, invert, arith, pass, 1'b0, alu__out
  // four_bit_reg accumulator: pin names not known; wires that end beside it: alu__out, load__acc, reset, clk, accum
  // four_bit_mux accum__mux: pin names not known; wires that end beside it: accum__mux_p1, accum, acc__to__db, data__bus
  program_ram program_ram_1 (
    .addr(addr__bus), .data__in(data__bus), .clk(clk), .write(write), .data__out(program_ram_1_data__out));
  // four_bit_mux data__mux: pin names not known; wires that end beside it: data__in, program_ram_1_data__out, read, accum__mux_p1
endmodule
