// Digital circuit program_ctr.dig as structural Verilog
module program_ctr (
  input  enable,
  input  reset,
  input  clk,
  output [3:0] q
);

  wire incrementer_1_p3;

  // incrementer incrementer_1: pin names not known; wires that end beside it: q, 1'b1, incrementer_1_p3
  // four_bit_reg four_bit_reg_1: pin names not known; wires that end beside it: incrementer_1_p3, enable, reset, clk, q
endmodule
